// Logisim project 王永辉_CS1405_U201414684_alu.circ as structural Verilog: 10 circuits, main circuit ALU
module ALU (
  input  [31:0] X,
  input  [31:0] Y,
  input  [3:0] AluOP,
  input  Cin,
  input  Cin_2,
  input  [15:0] A,
  input  [15:0] B,
  input  [31:0] A_2,
  input  [31:0] B_2,
  input  Cin_3,
  input  [3:0] A_3,
  input  [3:0] B_3,
  output Signed_Overflow,
  output UnSigned_Overflow,
  output Equal,
  output [31:0] Result,
  output [31:0] Result_2,
  output F,
  output F_2,
  output F_3,
  output F_4,
  output F_5,
  output F_6,
  output F_7,
  output F_8,
  output F_9,
  output F_10,
  output F_11,
  output F_12,
  output F_13,
  output F_14,
  output F_15,
  output F_16,
  output [31:0] F_17,
  output Cout,
  output Cout_2,
  output F0,
  output F2,
  output F1,
  output F0_2,
  output Cout_3
);

  // Probe on X
  // Probe on X
  // Probe on Y
  // Probe on Y
  // Probe on AluOP
  MyALU myalu_1 (
    .X(X), .Y(Y), .Result(Result), .UOF(UnSigned_Overflow), .OF(Signed_Overflow), .Equal(Equal),
    .Result2(Result_2), .OP(AluOP));
  // Probe on Result
  // Probe on Result
  thirtytwoBitsALU thirtytwobitsalu_1 (.A(A_2), .B(B_2), .Cin(Cin_2), .C2(F_17), .Cout(Cout_2));
  // Probe on Result_2
  FourBitALU fourbitalu_1 (
    .C4(Cout_3), .A_2(A_3), .A(Cin_3), .A_3(B_3), .F3(F0), .F2(F2), .F1(F1), .F0(F0_2));  // open: P, G
  sixteenBitALU sixteenbitalu_1 (
    .A(A), .B(B), .C0(Cin), .F15(F), .F14(F_2), .F13(F_3), .F7(F_9), .F12(F_4), .F6(F_10), .F5(F_11),
    .F4(F_12), .F11(F_5), .F10(F_6), .F9(F_7), .F3(F_13), .F8(F_8), .F2(F_14), .F1(F_15), .F0(F_16),
    .Cout(Cout));  // open: P, G

  // Other names for the same wires on the sheet: OF = Signed_Overflow; Result2[31:0] = Result_2; S[3:0] = AluOP;
  //   UOF = UnSigned_Overflow

  // Notes on the sheet:
  //   不要改变此引脚区域内容，也不要改变ALU封装形式
  //   输入引脚
  //   请在下方利用上方输入输出引脚的隧道信号构建ALU电路，ctrl+d复制选择部件
  //   华中科技大学计算机学院 计算机组成原理，鸣谢加州大学伯克利CS61C课程
  //   输出引脚
  //   探测区域
endmodule

module \演示电路  (
  input  [31:0] X,
  input  [31:0] Y,
  input  [3:0] ALUOP,
  output Signed_Overflow,
  output Unsigned_overflow,
  output [31:0] Result,
  output [31:0] Result_2,
  output Equal
);

  // Probe on X
  // Probe on X
  // ALU alu_1: pin names not known; wires that end beside it: X, Y, Signed_Overflow, ALUOP, ALUOP, ALUOP, ALUOP, ALUOP, ALUOP, ALUOP, Y, Unsigned_overflow, Equal, Equal, Result, Result_2, Result, Result_2, Result, Result_2, Result, Result_2, Result, Result_2, Result, Result, Result, Result, Result, Result, Result, Result, Result, Result, Result, Result, Result
  // Probe on ALUOP
  // Probe on Y
  // Probe on Y
  // Probe on Result
  // Probe on Result
  // Probe on Result_2

  // Notes on the sheet:
  //   ALu电路无需调整位置即可连接在该电路中，并且不能出现蓝色线缆和三态输出
endmodule

module \等差数列  (
  input  [31:0] \数列初始值 ,
  input  [31:0] \等差值 ,
  input  \时钟 ,
  output [31:0] Result
);

  // Probe on \数列初始值 
  // Probe on \数列初始值 
  // Probe on \等差值 
  // Probe on \等差值 
  // Probe on Result
  // Probe on Result

  // Other names for the same wires on the sheet: 数列初值[31:0] = \数列初始值 ; 累加和[31:0] = Result

  // Notes on the sheet:
  //   不要改变此引脚区域内容，也不要改变ALU封装形式
  //   请在下方利用上方输入输出引脚的隧道信号构建等差数列求和电路，ctrl+d复制选择部件
  //   华中科技大学计算机学院 计算机组成原理，鸣谢加州大学伯克利CS61C课程
  //   输出引脚
  //   探测区域
endmodule

// ll
module MyALU (
  input  [3:0] OP,
  input  [31:0] X,
  input  [31:0] Y,
  output [31:0] Result,
  output UOF,
  output OF,
  output Equal,
  output [31:0] Result2
);

  wire and_1_out, and_2_out, and_6_out, and_7_out, not_1_out, not_2_out, not_4_out, not_5_out, not_6_out,
       not_7_out, OFUOF, or_1_out, thirtytwobitsalu_1_cout, xor_2_out;
  wire [0:0] comparator_1_lt, comparator_2_lt;
  wire [30:0] multiplexer_1_out;
  wire [31:0] and_3_out, divider_1_out, divider_1_rem, multiplier_1_cout, multiplier_1_out, nor_1_out,
       not_3_out, or_2_out, shifter_1_out, shifter_2_out, shifter_3_out, thirtytwobitsalu_1_c2, xor_1_out;
  wire [31:31] multiplexer_1_out_2;

  and and_1 (and_1_out, not_4_out, X[31], multiplexer_1_out_2[31]);
  not not_1 (not_1_out, X[31]);
  not not_2 (not_2_out, multiplexer_1_out_2[31]);
  assign not_3_out = ~Y;  // NOT_Gate not_3, 32 bits wide
  Shifter #(.width(32)) shifter_1 (.in(X), .\dist (Y[4:0]), .out(shifter_1_out));
  Shifter #(.width(32), .shift("ar")) shifter_2 (.in(X), .\dist (Y[4:0]), .out(shifter_2_out));
  Shifter #(.width(32), .shift("lr")) shifter_3 (.in(X), .\dist (Y[4:0]), .out(shifter_3_out));
  Multiplier #(.width(32)) multiplier_1 (.a(X), .b(Y), .out(multiplier_1_out), .cout(multiplier_1_cout));  // open: cin
  Divider #(.width(32)) divider_1 (.a(X), .b(Y), .out(divider_1_out), .rem(divider_1_rem));  // open: upper
  and and_2 (and_2_out, thirtytwobitsalu_1_c2[31], not_1_out, not_2_out);
  Multiplexer #(.width(32), .disabled(0), .enable("false")) multiplexer_1 (
    .in0(Y), .in1(not_3_out), .out({multiplexer_1_out_2[31], multiplexer_1_out}), .sel(OP[1]));
  not not_4 (not_4_out, thirtytwobitsalu_1_c2[31]);
  or or_1 (or_1_out, and_1_out, and_2_out);
  thirtytwoBitsALU thirtytwobitsalu_1 (
    .A(X), .B({multiplexer_1_out_2[31], multiplexer_1_out}), .Cin(OP[1]), .C2(thirtytwobitsalu_1_c2),
    .Cout(thirtytwobitsalu_1_cout));
  assign and_3_out = X & Y;  // AND_Gate and_3, 32 bits wide
  assign or_2_out = X | Y;  // OR_Gate or_2, 32 bits wide
  assign xor_1_out = X ^ Y;  // XOR_Gate xor_1, 32 bits wide
  assign nor_1_out = ~(X | Y);  // NOR_Gate nor_1, 32 bits wide
  Comparator #(.width(32)) comparator_1 (.a(X), .b(Y), .lt(comparator_1_lt[0]));  // open: gt, eq
  Comparator #(.width(32), .mode("unsigned")) comparator_2 (.a(X), .b(Y), .lt(comparator_2_lt[0]));  // open: gt, eq
  and and_4 (UOF, OFUOF, xor_2_out);
  xor xor_2 (xor_2_out, thirtytwobitsalu_1_cout, OP[1]);
  and and_5 (OF, OFUOF, or_1_out);
  nor nor_2 (Equal, xor_1_out[0], xor_1_out[1], xor_1_out[2], xor_1_out[3], xor_1_out[4], xor_1_out[5], xor_1_out[6], xor_1_out[7], xor_1_out[8], xor_1_out[9], xor_1_out[10], xor_1_out[11], xor_1_out[12], xor_1_out[13], xor_1_out[14], xor_1_out[15], xor_1_out[17], xor_1_out[18], xor_1_out[19], xor_1_out[20], xor_1_out[21], xor_1_out[22], xor_1_out[23], xor_1_out[24], xor_1_out[25], xor_1_out[26], xor_1_out[27], xor_1_out[28], xor_1_out[29], xor_1_out[30], xor_1_out[31], xor_1_out[16]);
  not not_5 (not_5_out, OP[0]);
  not not_6 (not_6_out, OP[1]);
  Multiplexer #(.select(4), .width(32), .disabled(0), .enable("false")) multiplexer_2 (
    .in0(shifter_1_out), .in1(shifter_2_out), .in2(shifter_3_out), .in3(multiplier_1_out),
    .in4(divider_1_out), .in5(thirtytwobitsalu_1_c2), .in6(thirtytwobitsalu_1_c2), .in7(and_3_out),
    .in8(or_2_out), .in9(xor_1_out), .in10(nor_1_out), .in11({{31{1'b0}}, comparator_1_lt[0]}),
    .in12({{31{1'b0}}, comparator_2_lt[0]}), .in13({32{1'b0}}), .in14({32{1'b0}}), .in15({32{1'b0}}),
    .out(Result), .sel(OP));
  Multiplexer #(.select(4), .width(32), .disabled(0), .enable("false")) multiplexer_3 (
    .in0({32{1'b0}}), .in1({32{1'b0}}), .in2({32{1'b0}}), .in3(multiplier_1_cout), .in4(divider_1_rem),
    .in5({32{1'b0}}), .in6({32{1'b0}}), .in7({32{1'b0}}), .in8({32{1'b0}}), .in9({32{1'b0}}),
    .in10({32{1'b0}}), .in11({32{1'b0}}), .in12({32{1'b0}}), .in13({32{1'b0}}), .in14({32{1'b0}}),
    .in15({32{1'b0}}), .out(Result2), .sel(OP));
  or or_3 (OFUOF, and_6_out, and_7_out);
  not not_7 (not_7_out, OP[3]);
  and and_6 (and_6_out, OP[0], not_6_out, not_7_out, not_7_out);
  and and_7 (and_7_out, not_5_out, OP[1], OP[2], not_7_out);
endmodule

module thirtytwoBitsALU (
  input  [31:0] A,
  input  [31:0] B,
  input  Cin,
  output Cout,
  output [31:0] C2
);

  wire _0_g, _0_p, parallelcarry16bits_1_c4, sixteenbitalu_1_g, sixteenbitalu_1_p;

  parallelCarry16Bits parallelcarry16bits_1 (
    .C8(Cout), .C4(parallelcarry16bits_1_c4), .G3(1'b0), .P3(1'b0), .G2(1'b0), .P2(1'b0),
    .G1(sixteenbitalu_1_g), .P1(sixteenbitalu_1_p), .G0(_0_g), .P0(_0_p), .C0(Cin));  // open: P, G, C16, C12
  sixteenBitALU sixteenbitalu_1 (
    .A(A[31:16]), .B(B[31:16]), .C0(parallelcarry16bits_1_c4), .F15(C2[31]), .F14(C2[30]), .F13(C2[29]),
    .F7(C2[23]), .F12(C2[28]), .F6(C2[22]), .F5(C2[21]), .F4(C2[20]), .F11(C2[27]), .F10(C2[26]),
    .F9(C2[25]), .F3(C2[19]), .F8(C2[24]), .F2(C2[18]), .F1(C2[17]), .F0(C2[16]), .P(sixteenbitalu_1_p),
    .G(sixteenbitalu_1_g));  // open: Cout
  sixteenBitALU _0 (
    .A(A[15:0]), .B(B[15:0]), .C0(Cin), .F15(C2[15]), .F14(C2[14]), .F13(C2[13]), .F7(C2[7]), .F12(C2[12]),
    .F6(C2[6]), .F5(C2[5]), .F4(C2[4]), .F11(C2[11]), .F10(C2[10]), .F9(C2[9]), .F3(C2[3]), .F8(C2[8]),
    .F2(C2[2]), .F1(C2[1]), .F0(C2[0]), .P(_0_p), .G(_0_g));  // open: Cout

  // Notes on the sheet:
  //   1
endmodule

module sixteenBitALU (
  input  C0,
  input  [15:0] A,
  input  [15:0] B,
  output G,
  output P,
  output Cout,
  output F13,
  output F15,
  output F14,
  output F12,
  output F11,
  output F10,
  output F9,
  output F8,
  output F3,
  output F2,
  output F1,
  output F0,
  output F4,
  output F7,
  output F6,
  output F5
);

  wire _0_g, _0_p, _1_g, _1_p, _2_g, _2_p, _3_g, _3_p, parallelcarry16bits_1_c4, parallelcarry16bits_1_c8,
       parallelcarry16bits_1_c12;

  FourBitALU _3 (
    .A_2(A[15:12]), .A(parallelcarry16bits_1_c12), .A_3(B[15:12]), .F3(F15), .F2(F14), .F1(F13), .F0(F12),
    .P(_3_p), .G(_3_g));  // open: C4
  FourBitALU _1 (
    .A_2(A[7:4]), .A(parallelcarry16bits_1_c4), .A_3(B[7:4]), .F3(F7), .F2(F6), .F1(F5), .F0(F4), .P(_1_p),
    .G(_1_g));  // open: C4
  parallelCarry16Bits parallelcarry16bits_1 (
    .P(P), .G(G), .C16(Cout), .C12(parallelcarry16bits_1_c12), .C8(parallelcarry16bits_1_c8),
    .C4(parallelcarry16bits_1_c4), .G3(_3_g), .P3(_3_p), .G2(_2_g), .P2(_2_p), .G1(_1_g), .P1(_1_p),
    .G0(_0_g), .P0(_0_p), .C0(C0));
  FourBitALU _2 (
    .A_2(A[11:8]), .A(parallelcarry16bits_1_c8), .A_3(B[11:8]), .F3(F11), .F2(F10), .F1(F9), .F0(F8),
    .P(_2_p), .G(_2_g));  // open: C4
  FourBitALU _0 (
    .A_2(A[3:0]), .A(C0), .A_3(B[3:0]), .F3(F3), .F2(F2), .F1(F1), .F0(F0), .P(_0_p), .G(_0_g));  // open: C4
endmodule

module FourBitALU (
  input  A,
  input  [3:0] A_2,
  input  [3:0] A_3,
  output G,
  output P,
  output F3,
  output F2,
  output F1,
  output F0,
  output C4
);

  wire parallelcarry_1_c1, parallelcarry_1_c2, parallelcarry_1_c3;

  FA fa_1 (.A(A_3[3]), .B(A_2[3]), .Cin(parallelcarry_1_c3), .F(F3));  // open: Cout
  FA fa_2 (.A(A_3[2]), .B(A_2[2]), .Cin(parallelcarry_1_c2), .F(F2));  // open: Cout
  parallelCarry parallelcarry_1 (
    .Cin(A), .C4(C4), .C3(parallelcarry_1_c3), .C2(parallelcarry_1_c2), .C1(parallelcarry_1_c1), .A(A_3),
    .B(A_2), .G(G), .P(P));
  FA fa_3 (.A(A_3[1]), .B(A_2[1]), .Cin(parallelcarry_1_c1), .F(F1));  // open: Cout
  FA fa_4 (.A(A_3[0]), .B(A_2[0]), .Cin(A), .F(F0));  // open: Cout
endmodule

module parallelCarry16Bits (
  input  G3,
  input  P3,
  input  G2,
  input  P2,
  input  G1,
  input  P1,
  input  G0,
  input  P0,
  input  C0,
  output G,
  output C16,
  output C12,
  output C8,
  output C4,
  output P
);

  wire and_2_out, and_3_out, and_4_out, and_5_out, and_6_out, and_7_out, and_8_out, and_9_out, and_10_out,
       and_11_out;

  and and_1 (P, P3, P2, P1, P0);
  or or_1 (G, and_2_out, G3, and_4_out, and_3_out);
  or or_2 (C16, G3, and_2_out, and_4_out, and_3_out, and_6_out);
  and and_2 (and_2_out, P3, P2, G1);
  and and_3 (and_3_out, P3, G2);
  and and_4 (and_4_out, P3, G0, P2, P1);
  and and_5 (and_5_out, P2, G1);
  and and_6 (and_6_out, P3, C0, P2, P1, P0);
  or or_3 (C12, and_5_out, G2, and_7_out, and_8_out);
  and and_7 (and_7_out, P2, G0, P1);
  and and_8 (and_8_out, P2, P0, P1, C0);
  or or_4 (C8, G1, and_9_out, and_10_out);
  and and_9 (and_9_out, P1, G0);
  and and_10 (and_10_out, P1, P0, C0);
  or or_5 (C4, G0, and_11_out);
  and and_11 (and_11_out, P0, C0);
endmodule

module parallelCarry (
  input  Cin,
  input  [3:0] A,
  input  [3:0] B,
  output P,
  output G,
  output C4,
  output C3,
  output C2,
  output C1
);

  wire and_2_out, and_3_out, and_4_out, and_5_out, and_6_out, and_7_out, and_8_out, and_9_out, and_10_out,
       and_11_out, and_12_out, and_13_out, and_14_out, and_15_out, or_3_out, or_5_out, or_7_out, or_9_out;

  and and_1 (P, or_3_out, or_9_out, or_7_out, or_5_out);
  or or_1 (G, and_6_out, and_2_out, and_3_out, and_5_out);
  and and_2 (and_2_out, or_3_out, and_9_out);
  or or_2 (C4, and_6_out, and_2_out, and_3_out, and_5_out, and_4_out);
  and and_3 (and_3_out, or_3_out, or_5_out, and_12_out);
  and and_4 (and_4_out, or_3_out, or_9_out, or_7_out, or_5_out, Cin);
  and and_5 (and_5_out, or_3_out, or_7_out, or_5_out, and_14_out);
  and and_6 (and_6_out, A[3], B[3]);
  and and_7 (and_7_out, or_5_out, and_12_out);
  or or_3 (or_3_out, A[3], B[3]);
  or or_4 (C3, and_7_out, and_9_out, and_8_out, and_10_out);
  and and_8 (and_8_out, and_14_out, or_7_out, or_5_out);
  or or_5 (or_5_out, A[2], B[2]);
  and and_9 (and_9_out, A[2], B[2]);
  and and_10 (and_10_out, or_5_out, or_9_out, or_7_out, Cin);
  or or_6 (C2, and_12_out, and_11_out, and_13_out);
  and and_11 (and_11_out, or_7_out, and_14_out);
  and and_12 (and_12_out, A[1], B[1]);
  and and_13 (and_13_out, or_7_out, or_9_out, Cin);
  or or_7 (or_7_out, A[1], B[1]);
  or or_8 (C1, and_14_out, and_15_out);
  or or_9 (or_9_out, A[0], B[0]);
  and and_14 (and_14_out, A[0], B[0]);
  and and_15 (and_15_out, or_9_out, Cin);
endmodule

module FA (
  input  A,
  input  B,
  input  Cin,
  output F,
  output Cout
);

  wire and_1_out, and_2_out, and_3_out, xor_1_out;

  xor xor_1 (xor_1_out, A, B);
  and and_1 (and_1_out, A, B);
  and and_2 (and_2_out, A, Cin);
  and and_3 (and_3_out, B, Cin);
  xor xor_2 (F, xor_1_out, Cin);
  or or_1 (Cout, and_1_out, and_2_out, and_3_out);
endmodule
