// Logisim project 王永辉_CS1405_U201414684_cpu.circ as structural Verilog: 11 circuits, main circuit main
module main (
);

  wire a_1_branch, a_1_brancha, a_1_memread, a_1_memwrite, a_1_out_10, a_1_regdst2, and_2_out, and_3_out,
       and_5_out, bgez_1_jump_control, Clk, clock_1_out, comparator_1_eq, comparator_2_eq, comparator_2_gt,
       halt, imme_extent_1_extent_out, multiplexer_4_out, myalu_1_equal, nor_1_out, nor_2_out, not_1_out,
       not_2_out, not_3_out, or_1_out, or_2_out, register_1_q;
  wire [1:0] a_1_aluop, a_1_alusrc, a_1_jump, a_1_memtoreg, a_1_regdst, bgez_1_jump, multiplexer_8_out;
  wire [3:0] aluin_comtrol_1_aluin, myregfile_1_a0, myregfile_1_a0_3, myregfile_1_a0_4;
  wire [4:0] multiplexer_2_out, multiplexer_3_out;
  wire [5:0] funct_control_1_ofunct;
  wire [7:0] ram_1_data;
  wire [9:0] counter_1_q_2;
  wire [25:0] shifter_1_out;
  wire [31:0] adder_1_out, adder_2_out, counter_1_q, counter_2_q, multiplexer_5_out, multiplexer_6_out,
       multiplexer_7_out, multiplexer_9_out, myalu_1_result, myregfile_1_r1, myregfile_1_r2, myregfile_1_v0,
       rom_1_data, shifter_2_out;
  wire [31:4] myregfile_1_a0_2;
  wire [31:8] ram_1_data_2;
  wire [31:31] and_1_out;

  Clock clock_1 (.out(clock_1_out));
  Multiplexer #(.disabled(0), .enable("false")) multiplexer_1 (.in0(clock_1_out), .in1(1'b0), .out(Clk), .sel(halt));
  Register #(.width(1)) register_1 (.D(halt), .en(1'b1), .Q(register_1_q), .clk(clock_1_out), .clr(1'b0));
  or or_1 (or_1_out, register_1_q, Clk);
  Counter #(.width(32), .max('hffffffff)) counter_1 (
    .load(1'b1), .D(multiplexer_7_out), .count(1'b0),
    .Q({counter_1_q[31:12], counter_1_q_2, counter_1_q[1:0]}), .clk(Clk), .clr(1'b0));  // open: carry
  Adder #(.width(32)) adder_1 (
    .a(32'h4), .b({counter_1_q[31:12], counter_1_q_2, counter_1_q[1:0]}), .out(adder_1_out), .cin(1'b0));  // open: cout
  Counter #(.width(32), .max('hffffffff)) counter_2 (
    .load(1'b0), .D({32{1'b0}}), .count(1'b1), .Q(counter_2_q), .clk(or_1_out), .clr(1'b0));  // open: carry
  // Probe on counter_2_q
  ROM #(.addrWidth(10), .dataWidth(32)) rom_1 (.addr(counter_1_q_2), .data(rom_1_data), .sel(1'b1));
  Imme_extent imme_extent_1 (.OP(rom_1_data[31:26]), .extent_out(imme_extent_1_extent_out));
  and and_1 (and_1_out[31], imme_extent_1_extent_out, rom_1_data[15]);
  Shifter #(.width(26)) shifter_1 (.in(rom_1_data[25:0]), .\dist (5'b00010), .out(shifter_1_out));
  a a_1 (
    .OP(rom_1_data[31:26]), .Funct(rom_1_data[5:0]), .Branch(a_1_branch), .Jump(a_1_jump),
    .RegDst(a_1_regdst), .MemtoReg(a_1_memtoreg), .RegDst2(a_1_regdst2), .Brancha(a_1_brancha),
    .ALUsrc(a_1_alusrc), .ALUop(a_1_aluop), .MemRead(a_1_memread), .MemWrite(a_1_memwrite),
    .out_10(a_1_out_10));
  Multiplexer #(.width(5), .disabled(0), .enable("false")) multiplexer_2 (
    .in0(rom_1_data[25:21]), .in1(rom_1_data[20:16]), .out(multiplexer_2_out), .sel(a_1_regdst2));
  Multiplexer #(.select(2), .width(5), .disabled(0), .enable("false")) multiplexer_3 (
    .in0(rom_1_data[20:16]), .in1(rom_1_data[15:11]), .in2({5{1'b1}}), .in3({5{1'b0}}),
    .out(multiplexer_3_out), .sel(a_1_regdst));
  funct_control funct_control_1 (.OP(rom_1_data[31:26]), .Funct(rom_1_data[5:0]), .Ofunct(funct_control_1_ofunct));
  not not_1 (not_1_out, rom_1_data[2]);
  not not_2 (not_2_out, rom_1_data[3]);
  MyRegfile myregfile_1 (
    .WE(a_1_out_10), .R1(myregfile_1_r1), .R2(myregfile_1_r2), .W_num(multiplexer_3_out),
    .Din(multiplexer_9_out), .R1_num(multiplexer_2_out), .R2_num(rom_1_data[20:16]), .CLK(Clk),
    .a0({myregfile_1_a0_2[31:16], myregfile_1_a0_4, myregfile_1_a0_3, myregfile_1_a0_2[7:4], myregfile_1_a0}),
    .v0(myregfile_1_v0));  // open: S0, S1, S2, ra
  nor nor_1 (nor_1_out, rom_1_data[26], rom_1_data[27], rom_1_data[28], rom_1_data[30], rom_1_data[31], rom_1_data[29]);
  nor nor_2 (nor_2_out, rom_1_data[0], rom_1_data[1], not_1_out, rom_1_data[4], rom_1_data[5], not_2_out);
  Adder #(.width(32)) adder_2 (.a(adder_1_out), .b(shifter_2_out), .out(adder_2_out), .cin(1'b0));  // open: cout
  Shifter #(.width(32)) shifter_2 (
    .in({{16{and_1_out[31]}}, rom_1_data[15:0]}), .\dist (5'b00010), .out(shifter_2_out));
  and and_2 (and_2_out, nor_1_out, nor_2_out);
  and and_3 (and_3_out, a_1_branch, multiplexer_4_out);
  Multiplexer #(.disabled(0), .enable("false")) multiplexer_4 (
    .in0(myalu_1_equal), .in1(not_3_out), .out(multiplexer_4_out), .sel(a_1_brancha));
  not not_3 (not_3_out, myalu_1_equal);
  MyALU myalu_1 (
    .X(myregfile_1_r1), .Y(multiplexer_5_out), .Result(myalu_1_result), .Equal(myalu_1_equal),
    .OP(aluin_comtrol_1_aluin));  // open: UOF, OF, Result2
  Multiplexer #(.select(2), .width(32), .disabled(0), .enable("false")) multiplexer_5 (
    .in0(myregfile_1_r2), .in1({{16{and_1_out[31]}}, rom_1_data[15:0]}),
    .in2({{27{1'b0}}, rom_1_data[10:6]}), .in3({rom_1_data[15:0], {16{1'b0}}}), .out(multiplexer_5_out),
    .sel(a_1_alusrc));
  ALUin_comtrol aluin_comtrol_1 (.ALUop(a_1_aluop), .Funct(funct_control_1_ofunct), .ALUin(aluin_comtrol_1_aluin));
  Comparator #(.width(32)) comparator_1 (.a(myregfile_1_v0), .b(32'ha), .eq(comparator_1_eq));  // open: gt, lt
  Multiplexer #(.width(32), .disabled(0), .enable("false")) multiplexer_6 (
    .in0(adder_1_out), .in1(adder_2_out), .out(multiplexer_6_out), .sel(and_3_out));
  Hex_Digit_Display hex_digit_display_1 (.value(myregfile_1_a0_2[31:28]), .dp(1'b0));
  and and_4 (halt, comparator_1_eq, and_2_out);
  Multiplexer #(.select(2), .width(32), .disabled(0), .enable("false")) multiplexer_7 (
    .in0(multiplexer_6_out), .in1({adder_1_out[31:28], rom_1_data[25:24], shifter_1_out}),
    .in2(myregfile_1_r1), .in3(adder_2_out), .out(multiplexer_7_out), .sel(multiplexer_8_out));
  Multiplexer #(.width(2), .disabled(0), .enable("false")) multiplexer_8 (
    .in0(a_1_jump), .in1(bgez_1_jump), .out(multiplexer_8_out), .sel(and_5_out));
  Hex_Digit_Display hex_digit_display_2 (.value(myregfile_1_a0_2[27:24]), .dp(1'b0));
  Hex_Digit_Display hex_digit_display_3 (.value(myregfile_1_a0_2[23:20]), .dp(1'b0));
  Bgez bgez_1 (.op(rom_1_data[31:26]), .rt(rom_1_data[20:16]), .jump(bgez_1_jump), .jump_control(bgez_1_jump_control));
  Hex_Digit_Display hex_digit_display_4 (.value(myregfile_1_a0_4), .dp(1'b0));
  Hex_Digit_Display hex_digit_display_5 (.value(myregfile_1_a0_2[19:16]), .dp(1'b0));
  Comparator #(.width(32)) comparator_2 (
    .a(myregfile_1_r1), .b({32{1'b0}}), .gt(comparator_2_gt), .eq(comparator_2_eq));  // open: lt
  RAM #(.addrWidth(10), .dataWidth(32), .bus("separate")) ram_1 (
    .addr(myalu_1_result[11:2]), .din(myregfile_1_r2), .data({ram_1_data_2, ram_1_data}), .str(a_1_memwrite),
    .sel(1'b1), .clk(Clk), .ld(a_1_memread), .clr(1'b0));
  Hex_Digit_Display hex_digit_display_6 (.value(myregfile_1_a0_3), .dp(1'b0));
  // Probe on {myregfile_1_a0_2[31:16], myregfile_1_a0_4, myregfile_1_a0_3, myregfile_1_a0_2[7:4], myregfile_1_a0}
  and and_5 (and_5_out, bgez_1_jump_control, or_2_out);
  or or_2 (or_2_out, comparator_2_gt, comparator_2_eq);
  Multiplexer #(.select(2), .width(32), .disabled(0), .enable("false")) multiplexer_9 (
    .in0({ram_1_data_2, ram_1_data}), .in1(myalu_1_result), .in2(adder_1_out),
    .in3({{24{1'b0}}, ram_1_data}), .out(multiplexer_9_out), .sel(a_1_memtoreg));
  Hex_Digit_Display hex_digit_display_7 (.value(myregfile_1_a0), .dp(1'b0));
  Hex_Digit_Display hex_digit_display_8 (.value(myregfile_1_a0_2[7:4]), .dp(1'b0));

  // Notes on the sheet:
  //   PC
  //   contents of rom_1 (hex, n*v repeats v):
  //   24160003 20090001 201300ff 132020 20020022 c 201400fd 142020 20020022 c 2749823 132020 20020022 c
  //   20131234 132020 20020022 c 3c131234 132020 20020022 c 3c011234 34215678 19820 132020 20020022 c
  //   ac130014 90130014 132020 20020022 c 20130010 132020 20020022 c 6610004 20040666 20020022 c 800002f
  //   3c010000 34218888 12020 20020022 c 2013ffff 132020 20020022 c 6610004 20040666 20020022 c 800003d
  //   3c010000 34218888 12020 20020022 c 2c9b022 12c00001 8000001 2002000a c
  //   RegDst
  //   addi/addiu
  //   Brancha
  //   RegWrite
  //   Branch
  //   ALUSrc
  //   lui
  //   bgez
  //   Jump
  //   bgez
  //   MemtoReg
  //   RAM
  //   MemRead
  //   MemWrite
endmodule

module funct_control (
  input  [5:0] OP,
  input  [5:0] Funct,
  output [5:0] Ofunct
);

  Funct_control funct_control_1 (
    .OP5(OP[5]), .OP4(OP[4]), .OP3(OP[3]), .OP2(OP[2]), .OP1(OP[1]), .OP0(OP[0]), .Funct5(Funct[5]),
    .Funct4(Funct[4]), .Funct3(Funct[3]), .Funct2(Funct[2]), .Funct1(Funct[1]), .Funct0(Funct[0]),
    .funct_out5(Ofunct[5]), .funct_out4(Ofunct[4]), .funct_out3(Ofunct[3]), .funct_out2(Ofunct[2]),
    .funct_out1(Ofunct[1]), .funct_out0(Ofunct[0]));

  // Notes on the sheet:
  //   用于封装
endmodule

module ALUin_comtrol (
  input  [1:0] ALUop,
  input  [5:0] Funct,
  output [3:0] ALUin
);

  aluin_control aluin_control_1 (
    .ALUop1(ALUop[1]), .ALUop0(ALUop[0]), .Funct5(Funct[5]), .ALUin3(ALUin[3]), .Funct4(Funct[4]),
    .Funct3(Funct[3]), .Funct2(Funct[2]), .Funct1(Funct[1]), .Funct0(Funct[0]), .ALUin2(ALUin[2]),
    .ALUin1(ALUin[1]), .ALUin0(ALUin[0]));

  // Notes on the sheet:
  //   用于封装
endmodule

module a (
  input  [5:0] OP,
  input  [5:0] Funct,
  output Branch,
  output [1:0] Jump,
  output [1:0] RegDst,
  output [1:0] MemtoReg,
  output RegDst2,
  output Brancha,
  output [1:0] ALUsrc,
  output out_10,
  output [1:0] ALUop,
  output MemRead,
  output MemWrite
);

  wire and_1_out, and_2_out, and_3_out, not_1_out, not_2_out, not_3_out, not_4_out, not_5_out, not_6_out,
       not_7_out, not_8_out, not_9_out;

  not not_1 (not_1_out, OP[5]);
  not not_2 (not_2_out, OP[4]);
  not not_3 (not_3_out, OP[2]);
  not not_4 (not_4_out, OP[3]);
  not not_5 (not_5_out, OP[4]);
  not not_6 (not_6_out, OP[2]);
  not not_7 (not_7_out, OP[4]);
  op_control_new op_control_new_1 (
    .OP31(OP[5]), .OP30(OP[4]), .Branch(Branch), .OP29(OP[3]), .OP28(OP[2]), .RegDst1(RegDst[1]),
    .OP27(OP[1]), .OP26(OP[0]), .f5(Funct[5]), .RegDst0(RegDst[0]), .f4(Funct[4]), .f3(Funct[3]),
    .f2(Funct[2]), .f1(Funct[1]), .Jump1(Jump[1]), .f0(Funct[0]), .Jump0(Jump[0]), .MemtoReg1(MemtoReg[1]),
    .MemtoReg0(MemtoReg[0]), .ALUsrc(ALUsrc[0]), .RegDst2(RegDst2), .Brancha(Brancha), .ALUop1(ALUop[1]),
    .RegWrite(out_10));
  and and_1 (and_1_out, not_1_out, not_2_out, OP[3], OP[1], OP[0], OP[2]);
  not not_8 (not_8_out, OP[0]);
  not not_9 (not_9_out, OP[1]);
  and and_2 (and_2_out, not_9_out, OP[2], not_8_out, not_4_out, not_5_out, OP[5]);
  and and_3 (and_3_out, OP[0], OP[1], not_3_out, not_4_out, not_5_out, OP[5]);
  and and_4 (MemWrite, OP[0], OP[1], not_6_out, OP[3], not_7_out, OP[5]);
  or or_1 (ALUsrc[1], RegDst2, and_1_out);
  or or_2 (MemRead, and_2_out, and_3_out);

  assign ALUop[0] = 1'b0;

  // Notes on the sheet:
  //   LUI
  //   lbu
  //   lw
endmodule

module op_control_new (
  input  OP31,
  input  OP30,
  input  OP29,
  input  OP28,
  input  OP27,
  input  OP26,
  input  f5,
  input  f4,
  input  f3,
  input  f2,
  input  f1,
  input  f0,
  output Branch,
  output RegDst1,
  output RegDst0,
  output Jump1,
  output Jump0,
  output MemtoReg1,
  output MemtoReg0,
  output ALUsrc,
  output RegDst2,
  output Brancha,
  output ALUop1,
  output RegWrite
);

  wire and_6_out, and_7_out, and_8_out, and_9_out, and_10_out, and_11_out, and_12_out, and_13_out,
       and_14_out, and_15_out, and_16_out, and_17_out, and_18_out, and_19_out, and_20_out, and_21_out,
       and_22_out, and_23_out, and_25_out, and_26_out, and_27_out, and_28_out, and_29_out, and_30_out,
       and_31_out, and_32_out, and_33_out, and_34_out, and_35_out, and_36_out, and_37_out, and_38_out,
       and_39_out, and_40_out, and_41_out, not_1_out, not_2_out, not_3_out, not_4_out, not_5_out, not_6_out,
       not_7_out, not_8_out, not_9_out, not_10_out, not_11_out, not_12_out, not_13_out, not_14_out,
       not_15_out, not_16_out, not_17_out, not_18_out, not_19_out, not_20_out, not_21_out, not_22_out,
       not_23_out, not_24_out, not_25_out, not_26_out, not_27_out, not_28_out, not_29_out, not_30_out,
       not_31_out, not_32_out, not_33_out, not_34_out, not_35_out, not_36_out, not_37_out, not_38_out,
       not_39_out, not_40_out, not_41_out, not_42_out, not_43_out, not_44_out, not_45_out, not_46_out,
       not_47_out, not_48_out, not_49_out, not_50_out, not_51_out, not_52_out, not_53_out, not_54_out,
       not_55_out, not_56_out, not_57_out, not_58_out, not_59_out, not_60_out, not_61_out, not_62_out,
       not_63_out, not_64_out, not_65_out, not_66_out, not_67_out, not_68_out, not_69_out, not_70_out,
       not_71_out, not_72_out, not_73_out, not_74_out, not_75_out, not_76_out, not_77_out, not_78_out,
       not_79_out, not_80_out, not_81_out, not_82_out, not_83_out, not_84_out, not_85_out, not_86_out,
       not_87_out, not_88_out, not_89_out, not_90_out, not_91_out, not_92_out, not_93_out, not_94_out,
       not_95_out, not_96_out, not_97_out, not_98_out, not_99_out, not_100_out, not_101_out, not_102_out,
       not_103_out, not_104_out, not_105_out, not_106_out, not_107_out, not_108_out, not_109_out,
       not_110_out, not_111_out, not_112_out, not_113_out, not_114_out, not_115_out, not_116_out,
       not_117_out, not_118_out, not_119_out, not_120_out, not_121_out, not_122_out, not_123_out,
       not_124_out, not_125_out, not_126_out, not_127_out, not_128_out, not_129_out, not_130_out,
       not_131_out, not_132_out, not_133_out, not_134_out, not_135_out, not_136_out, not_137_out,
       not_138_out, not_139_out, not_140_out, not_141_out, not_142_out, not_143_out, not_144_out,
       not_145_out, not_146_out, not_147_out, not_148_out, not_149_out, not_150_out, not_151_out,
       not_152_out, not_153_out, not_154_out, not_155_out, not_156_out, not_157_out, not_158_out,
       not_159_out, not_160_out, not_161_out, not_162_out, not_163_out, not_164_out, not_165_out,
       not_166_out, not_167_out, not_168_out, not_169_out, not_170_out, not_171_out, not_172_out,
       not_173_out, not_174_out, not_175_out, not_176_out, not_177_out, not_178_out, not_179_out,
       not_180_out, not_181_out, not_182_out, not_183_out, not_184_out, not_185_out, not_186_out,
       not_187_out, not_188_out, not_189_out, not_190_out, not_191_out, not_192_out, not_193_out,
       not_194_out, not_195_out, not_196_out, not_197_out, not_198_out, not_199_out, not_200_out,
       not_201_out, not_202_out, not_203_out, not_204_out, not_205_out, not_206_out, not_207_out,
       not_208_out, not_209_out, not_210_out, not_211_out, not_212_out, not_213_out, not_214_out,
       not_215_out, not_216_out, not_217_out, not_218_out, not_219_out, not_220_out, not_221_out,
       not_222_out, not_223_out, not_224_out, not_225_out, not_226_out, not_227_out, not_228_out,
       not_229_out, not_230_out, not_231_out, not_232_out, not_233_out, not_234_out, not_235_out;

  not not_1 (not_1_out, OP31);
  not not_2 (not_2_out, OP30);
  not not_3 (not_3_out, OP29);
  not not_4 (not_4_out, OP27);
  not not_5 (not_5_out, OP31);
  not not_6 (not_6_out, OP30);
  not not_7 (not_7_out, OP29);
  not not_8 (not_8_out, OP28);
  not not_9 (not_9_out, OP31);
  not not_10 (not_10_out, OP30);
  not not_11 (not_11_out, OP29);
  not not_12 (not_12_out, OP28);
  not not_13 (not_13_out, OP27);
  not not_14 (not_14_out, OP26);
  not not_15 (not_15_out, OP31);
  not not_16 (not_16_out, OP30);
  not not_17 (not_17_out, OP29);
  not not_18 (not_18_out, OP28);
  not not_19 (not_19_out, OP27);
  not not_20 (not_20_out, OP26);
  not not_21 (not_21_out, f5);
  not not_22 (not_22_out, f4);
  not not_23 (not_23_out, f2);
  not not_24 (not_24_out, f1);
  not not_25 (not_25_out, f0);
  not not_26 (not_26_out, OP31);
  not not_27 (not_27_out, OP30);
  not not_28 (not_28_out, OP29);
  not not_29 (not_29_out, OP28);
  not not_30 (not_30_out, OP31);
  not not_31 (not_31_out, OP30);
  not not_32 (not_32_out, OP29);
  not not_33 (not_33_out, OP28);
  not not_34 (not_34_out, OP30);
  not not_35 (not_35_out, OP29);
  not not_36 (not_36_out, OP27);
  not not_37 (not_37_out, OP26);
  not not_38 (not_38_out, OP31);
  not not_39 (not_39_out, OP30);
  not not_40 (not_40_out, OP28);
  not not_41 (not_41_out, OP27);
  not not_42 (not_42_out, OP26);
  not not_43 (not_43_out, f4);
  not not_44 (not_44_out, f3);
  not not_45 (not_45_out, f2);
  not not_46 (not_46_out, f0);
  not not_47 (not_47_out, OP31);
  not not_48 (not_48_out, OP30);
  not not_49 (not_49_out, OP28);
  not not_50 (not_50_out, OP27);
  not not_51 (not_51_out, OP26);
  not not_52 (not_52_out, f4);
  not not_53 (not_53_out, f3);
  not not_54 (not_54_out, f2);
  not not_55 (not_55_out, OP31);
  not not_56 (not_56_out, OP30);
  not not_57 (not_57_out, OP28);
  not not_58 (not_58_out, OP27);
  not not_59 (not_59_out, OP26);
  not not_60 (not_60_out, f4);
  not not_61 (not_61_out, f3);
  not not_62 (not_62_out, f1);
  not not_63 (not_63_out, OP31);
  not not_64 (not_64_out, OP30);
  not not_65 (not_65_out, OP28);
  not not_66 (not_66_out, OP27);
  not not_67 (not_67_out, OP26);
  not not_68 (not_68_out, f4);
  not not_69 (not_69_out, f3);
  not not_70 (not_70_out, OP31);
  not not_71 (not_71_out, OP30);
  not not_72 (not_72_out, OP28);
  not not_73 (not_73_out, OP27);
  not not_74 (not_74_out, OP26);
  not not_75 (not_75_out, f4);
  not not_76 (not_76_out, f2);
  not not_77 (not_77_out, OP31);
  not not_78 (not_78_out, OP30);
  not not_79 (not_79_out, OP28);
  not not_80 (not_80_out, OP26);
  not not_81 (not_81_out, OP31);
  not not_82 (not_82_out, OP30);
  not not_83 (not_83_out, OP27);
  not not_84 (not_84_out, OP31);
  not not_85 (not_85_out, OP30);
  not not_86 (not_86_out, OP30);
  not not_87 (not_87_out, OP29);
  not not_88 (not_88_out, OP27);
  not not_89 (not_89_out, OP26);
  not not_90 (not_90_out, OP31);
  not not_91 (not_91_out, OP30);
  not not_92 (not_92_out, OP28);
  not not_93 (not_93_out, OP26);
  not not_94 (not_94_out, OP31);
  not not_95 (not_95_out, OP30);
  not not_96 (not_96_out, OP27);
  not not_97 (not_97_out, OP31);
  not not_98 (not_98_out, OP30);
  not not_99 (not_99_out, OP30);
  not not_100 (not_100_out, OP28);
  not not_101 (not_101_out, OP30);
  not not_102 (not_102_out, OP29);
  not not_103 (not_103_out, OP27);
  not not_104 (not_104_out, OP26);
  not not_105 (not_105_out, OP31);
  not not_106 (not_106_out, OP30);
  not not_107 (not_107_out, OP29);
  not not_108 (not_108_out, OP28);
  not not_109 (not_109_out, OP27);
  not not_110 (not_110_out, OP26);
  not not_111 (not_111_out, f2);
  not not_112 (not_112_out, f5);
  not not_113 (not_113_out, f4);
  not not_114 (not_114_out, f3);
  not not_115 (not_115_out, f0);
  not not_116 (not_116_out, OP31);
  not not_117 (not_117_out, OP30);
  not not_118 (not_118_out, OP29);
  not not_119 (not_119_out, OP28);
  not not_120 (not_120_out, OP27);
  not not_121 (not_121_out, OP26);
  not not_122 (not_122_out, f2);
  not not_123 (not_123_out, f5);
  not not_124 (not_124_out, f4);
  not not_125 (not_125_out, f3);
  not not_126 (not_126_out, OP31);
  not not_127 (not_127_out, OP30);
  not not_128 (not_128_out, OP29);
  not not_129 (not_129_out, OP27);
  not not_130 (not_130_out, OP31);
  not not_131 (not_131_out, OP30);
  not not_132 (not_132_out, OP29);
  not not_133 (not_133_out, OP28);
  not not_134 (not_134_out, OP27);
  not not_135 (not_135_out, OP26);
  not not_136 (not_136_out, f4);
  not not_137 (not_137_out, f3);
  not not_138 (not_138_out, f2);
  not not_139 (not_139_out, f0);
  not not_140 (not_140_out, OP31);
  not not_141 (not_141_out, OP30);
  not not_142 (not_142_out, OP29);
  not not_143 (not_143_out, OP28);
  not not_144 (not_144_out, OP27);
  not not_145 (not_145_out, OP26);
  not not_146 (not_146_out, f4);
  not not_147 (not_147_out, f3);
  not not_148 (not_148_out, f2);
  not not_149 (not_149_out, OP31);
  not not_150 (not_150_out, OP30);
  not not_151 (not_151_out, OP29);
  not not_152 (not_152_out, OP28);
  not not_153 (not_153_out, OP27);
  not not_154 (not_154_out, OP26);
  not not_155 (not_155_out, f4);
  not not_156 (not_156_out, f3);
  not not_157 (not_157_out, f1);
  not not_158 (not_158_out, OP31);
  not not_159 (not_159_out, OP30);
  not not_160 (not_160_out, OP29);
  not not_161 (not_161_out, OP28);
  not not_162 (not_162_out, OP27);
  not not_163 (not_163_out, OP26);
  not not_164 (not_164_out, f4);
  not not_165 (not_165_out, f3);
  not not_166 (not_166_out, OP31);
  not not_167 (not_167_out, OP30);
  not not_168 (not_168_out, OP29);
  not not_169 (not_169_out, OP28);
  not not_170 (not_170_out, OP27);
  not not_171 (not_171_out, OP26);
  not not_172 (not_172_out, f4);
  not not_173 (not_173_out, f2);
  not not_174 (not_174_out, OP31);
  not not_175 (not_175_out, OP30);
  not not_176 (not_176_out, OP28);
  not not_177 (not_177_out, OP26);
  not not_178 (not_178_out, OP31);
  not not_179 (not_179_out, OP30);
  not not_180 (not_180_out, OP27);
  not not_181 (not_181_out, OP31);
  not not_182 (not_182_out, OP30);
  not not_183 (not_183_out, OP28);
  not not_184 (not_184_out, OP27);
  not not_185 (not_185_out, OP26);
  not not_186 (not_186_out, f4);
  not not_187 (not_187_out, f3);
  not not_188 (not_188_out, f2);
  not not_189 (not_189_out, f0);
  not not_190 (not_190_out, OP31);
  not not_191 (not_191_out, OP30);
  not not_192 (not_192_out, OP28);
  not not_193 (not_193_out, OP27);
  not not_194 (not_194_out, OP26);
  not not_195 (not_195_out, f4);
  not not_196 (not_196_out, f3);
  not not_197 (not_197_out, f2);
  not not_198 (not_198_out, OP31);
  not not_199 (not_199_out, OP30);
  not not_200 (not_200_out, OP28);
  not not_201 (not_201_out, OP27);
  not not_202 (not_202_out, OP26);
  not not_203 (not_203_out, f4);
  not not_204 (not_204_out, f3);
  not not_205 (not_205_out, f1);
  not not_206 (not_206_out, OP31);
  not not_207 (not_207_out, OP30);
  not not_208 (not_208_out, OP28);
  not not_209 (not_209_out, OP27);
  not not_210 (not_210_out, OP26);
  not not_211 (not_211_out, f4);
  not not_212 (not_212_out, f3);
  not not_213 (not_213_out, OP31);
  not not_214 (not_214_out, OP30);
  not not_215 (not_215_out, OP28);
  not not_216 (not_216_out, OP27);
  not not_217 (not_217_out, OP26);
  not not_218 (not_218_out, f4);
  not not_219 (not_219_out, f2);
  not not_220 (not_220_out, OP30);
  not not_221 (not_221_out, OP29);
  not not_222 (not_222_out, OP28);
  not not_223 (not_223_out, OP31);
  not not_224 (not_224_out, OP30);
  not not_225 (not_225_out, OP28);
  not not_226 (not_226_out, OP26);
  not not_227 (not_227_out, OP31);
  not not_228 (not_228_out, OP30);
  not not_229 (not_229_out, OP27);
  not not_230 (not_230_out, OP31);
  not not_231 (not_231_out, OP30);
  not not_232 (not_232_out, OP30);
  not not_233 (not_233_out, OP29);
  not not_234 (not_234_out, OP27);
  not not_235 (not_235_out, OP26);
  and and_1 (Branch, not_1_out, not_2_out, not_3_out, OP28, not_4_out);
  and and_2 (RegDst1, not_5_out, not_6_out, not_7_out, not_8_out, OP27, OP26);
  and and_3 (RegDst0, not_9_out, not_10_out, not_11_out, not_12_out, not_13_out, not_14_out);
  and and_4 (Jump1, not_15_out, not_16_out, not_17_out, not_18_out, not_19_out, not_20_out, not_21_out, not_22_out, f3, not_23_out, not_24_out, not_25_out);
  and and_5 (Jump0, not_26_out, not_27_out, not_28_out, not_29_out, OP27);
  and and_6 (and_6_out, not_30_out, not_31_out, not_32_out, not_33_out, OP27, OP26);
  and and_7 (and_7_out, OP31, not_34_out, not_35_out, OP28, not_36_out, not_37_out);
  and and_8 (and_8_out, not_38_out, not_39_out, not_40_out, not_41_out, not_42_out, not_43_out, not_44_out, not_45_out, not_46_out);
  and and_9 (and_9_out, not_47_out, not_48_out, not_49_out, not_50_out, not_51_out, not_52_out, not_53_out, not_54_out, f1);
  and and_10 (and_10_out, not_55_out, not_56_out, not_57_out, not_58_out, not_59_out, f5, not_60_out, not_61_out, not_62_out);
  and and_11 (and_11_out, not_63_out, not_64_out, not_65_out, not_66_out, not_67_out, f5, not_68_out, not_69_out, f0);
  and and_12 (and_12_out, not_70_out, not_71_out, not_72_out, not_73_out, not_74_out, f5, not_75_out, not_76_out, f1);
  and and_13 (and_13_out, not_77_out, not_78_out, OP29, not_79_out, not_80_out);
  and and_14 (and_14_out, not_81_out, not_82_out, OP29, not_83_out);
  and and_15 (and_15_out, not_84_out, not_85_out, OP29, OP28, OP26);
  and and_16 (and_16_out, OP31, not_86_out, not_87_out, OP28, not_88_out, not_89_out);
  and and_17 (and_17_out, not_90_out, not_91_out, OP29, not_92_out, not_93_out);
  and and_18 (and_18_out, not_94_out, not_95_out, OP29, not_96_out);
  and and_19 (and_19_out, not_97_out, not_98_out, OP29, OP28, OP26);
  and and_20 (and_20_out, OP31, not_99_out, not_100_out, OP27, OP26);
  and and_21 (and_21_out, OP31, not_101_out, not_102_out, OP28, not_103_out, not_104_out);
  and and_22 (and_22_out, not_105_out, not_106_out, not_107_out, not_108_out, not_109_out, not_110_out, not_111_out, not_112_out, not_113_out, not_114_out, not_115_out);
  and and_23 (and_23_out, not_116_out, not_117_out, not_118_out, not_119_out, not_120_out, not_121_out, not_122_out, not_123_out, not_124_out, not_125_out, f1);
  and and_24 (Brancha, not_126_out, not_127_out, not_128_out, OP28, not_129_out, OP26);
  and and_25 (and_25_out, not_130_out, not_131_out, not_132_out, not_133_out, not_134_out, not_135_out, not_136_out, not_137_out, not_138_out, not_139_out);
  and and_26 (and_26_out, not_140_out, not_141_out, not_142_out, not_143_out, not_144_out, not_145_out, not_146_out, not_147_out, not_148_out, f1);
  and and_27 (and_27_out, not_149_out, not_150_out, not_151_out, not_152_out, not_153_out, not_154_out, f5, not_155_out, not_156_out, not_157_out);
  and and_28 (and_28_out, not_158_out, not_159_out, not_160_out, not_161_out, not_162_out, not_163_out, f5, not_164_out, not_165_out, f0);
  and and_29 (and_29_out, not_166_out, not_167_out, not_168_out, not_169_out, not_170_out, not_171_out, f5, not_172_out, not_173_out, f1);
  and and_30 (and_30_out, not_174_out, not_175_out, OP29, not_176_out, OP27, not_177_out);
  and and_31 (and_31_out, not_178_out, not_179_out, OP29, OP28, not_180_out);
  and and_32 (and_32_out, not_181_out, not_182_out, not_183_out, not_184_out, not_185_out, not_186_out, not_187_out, not_188_out, not_189_out);
  and and_33 (and_33_out, not_190_out, not_191_out, not_192_out, not_193_out, not_194_out, not_195_out, not_196_out, not_197_out, f1);
  and and_34 (and_34_out, not_198_out, not_199_out, not_200_out, not_201_out, not_202_out, f5, not_203_out, not_204_out, not_205_out);
  and and_35 (and_35_out, not_206_out, not_207_out, not_208_out, not_209_out, not_210_out, f5, not_211_out, not_212_out, f0);
  and and_36 (and_36_out, not_213_out, not_214_out, not_215_out, not_216_out, not_217_out, f5, not_218_out, not_219_out, f1);
  and and_37 (and_37_out, not_220_out, not_221_out, not_222_out, OP27, OP26);
  and and_38 (and_38_out, not_223_out, not_224_out, OP29, not_225_out, not_226_out);
  and and_39 (and_39_out, not_227_out, not_228_out, OP29, not_229_out);
  and and_40 (and_40_out, not_230_out, not_231_out, OP29, OP28, OP26);
  and and_41 (and_41_out, OP31, not_232_out, not_233_out, OP28, not_234_out, not_235_out);
  or or_1 (MemtoReg1, and_6_out, and_7_out);
  or or_2 (MemtoReg0, and_8_out, and_9_out, and_10_out, and_11_out, and_12_out, and_13_out, and_14_out, and_15_out, and_16_out);
  or or_3 (ALUsrc, and_17_out, and_18_out, and_19_out, and_20_out, and_21_out);
  or or_4 (RegDst2, and_22_out, and_23_out);
  or or_5 (ALUop1, and_25_out, and_26_out, and_27_out, and_28_out, and_29_out, and_30_out, and_31_out);
  or or_6 (RegWrite, and_32_out, and_33_out, and_34_out, and_35_out, and_36_out, and_37_out, and_38_out, and_39_out, and_40_out, and_41_out);
endmodule

module Funct_control (
  input  OP5,
  input  OP4,
  input  OP3,
  input  OP2,
  input  OP1,
  input  OP0,
  input  Funct5,
  input  Funct4,
  input  Funct3,
  input  Funct2,
  input  Funct1,
  input  Funct0,
  output funct_out5,
  output funct_out4,
  output funct_out3,
  output funct_out2,
  output funct_out1,
  output funct_out0
);

  wire and_1_out, and_2_out, and_3_out, and_4_out, and_5_out, and_6_out, and_7_out, and_8_out, and_9_out,
       and_10_out, and_11_out, and_12_out, and_13_out, and_14_out, and_15_out, and_16_out, and_17_out,
       and_18_out, and_19_out, and_20_out, and_21_out, and_22_out, and_23_out, and_24_out, and_25_out,
       and_26_out, and_27_out, nor_1_out, nor_2_out, not_1_out, not_2_out, not_3_out, not_4_out, not_5_out,
       not_6_out, not_7_out, not_8_out, not_9_out, not_10_out, not_11_out, not_12_out, not_13_out,
       not_14_out, not_15_out, not_16_out, not_17_out, not_18_out, not_19_out, not_20_out, not_21_out,
       not_22_out, not_23_out, not_24_out, not_25_out, not_26_out, not_27_out, not_28_out, not_29_out,
       not_30_out, not_31_out, not_32_out, not_33_out, not_34_out, not_35_out, not_36_out, not_37_out,
       not_38_out, not_39_out, not_40_out, not_41_out, not_42_out, not_43_out, not_44_out, not_45_out,
       not_46_out, not_47_out, not_48_out, not_49_out, not_50_out, not_51_out, not_52_out, not_53_out,
       not_54_out, not_55_out, not_56_out, not_57_out, not_58_out, not_59_out, not_60_out, not_61_out,
       not_62_out, not_63_out, not_64_out, not_65_out, not_66_out, not_67_out, not_68_out, not_69_out,
       not_70_out, not_71_out, not_72_out, not_73_out, not_74_out, not_75_out, not_76_out, not_77_out,
       not_78_out, not_79_out, not_80_out, not_81_out, not_82_out, not_83_out, not_84_out, not_85_out,
       not_86_out, not_87_out, not_88_out, not_89_out, not_90_out, not_91_out, not_92_out, not_93_out,
       not_94_out, not_95_out, not_96_out, not_97_out, not_98_out, not_99_out, not_100_out, not_101_out,
       not_102_out, not_103_out, not_104_out, not_105_out, not_106_out, not_107_out, not_108_out,
       not_109_out, not_110_out, not_111_out, not_112_out, not_113_out, not_114_out, not_115_out,
       not_116_out, not_117_out, not_118_out, not_119_out, not_120_out, not_121_out, not_122_out,
       not_123_out, not_124_out, not_125_out, not_126_out, not_127_out, not_128_out, not_129_out,
       not_130_out, not_131_out, not_132_out, not_133_out, not_134_out, not_135_out, not_136_out,
       not_137_out, not_138_out, not_139_out, not_140_out, not_141_out, not_142_out, not_143_out,
       not_144_out, not_145_out, not_146_out, not_147_out, not_148_out, not_149_out, or_2_out, or_3_out;

  not not_1 (not_1_out, OP5);
  not not_2 (not_2_out, OP4);
  not not_3 (not_3_out, OP3);
  not not_4 (not_4_out, OP2);
  not not_5 (not_5_out, OP1);
  not not_6 (not_6_out, OP0);
  not not_7 (not_7_out, Funct5);
  not not_8 (not_8_out, Funct3);
  not not_9 (not_9_out, Funct2);
  not not_10 (not_10_out, Funct1);
  not not_11 (not_11_out, Funct0);
  not not_12 (not_12_out, OP5);
  not not_13 (not_13_out, OP4);
  not not_14 (not_14_out, OP3);
  not not_15 (not_15_out, OP2);
  not not_16 (not_16_out, OP1);
  not not_17 (not_17_out, OP0);
  not not_18 (not_18_out, Funct4);
  not not_19 (not_19_out, Funct3);
  not not_20 (not_20_out, Funct1);
  not not_21 (not_21_out, OP5);
  not not_22 (not_22_out, OP4);
  not not_23 (not_23_out, OP3);
  not not_24 (not_24_out, OP2);
  not not_25 (not_25_out, OP1);
  not not_26 (not_26_out, OP0);
  not not_27 (not_27_out, Funct4);
  not not_28 (not_28_out, Funct3);
  not not_29 (not_29_out, OP5);
  not not_30 (not_30_out, OP4);
  not not_31 (not_31_out, OP3);
  not not_32 (not_32_out, OP2);
  not not_33 (not_33_out, OP1);
  not not_34 (not_34_out, OP0);
  not not_35 (not_35_out, Funct4);
  not not_36 (not_36_out, Funct2);
  not not_37 (not_37_out, OP5);
  not not_38 (not_38_out, OP4);
  not not_39 (not_39_out, OP3);
  not not_40 (not_40_out, OP2);
  not not_41 (not_41_out, OP1);
  not not_42 (not_42_out, Funct4);
  not not_43 (not_43_out, Funct3);
  not not_44 (not_44_out, Funct2);
  not not_45 (not_45_out, OP5);
  not not_46 (not_46_out, OP4);
  not not_47 (not_47_out, OP2);
  not not_48 (not_48_out, OP0);
  not not_49 (not_49_out, OP5);
  not not_50 (not_50_out, OP4);
  not not_51 (not_51_out, OP1);
  not not_52 (not_52_out, Funct4);
  not not_53 (not_53_out, Funct2);
  not not_54 (not_54_out, Funct0);
  not not_55 (not_55_out, Funct4);
  not not_56 (not_56_out, Funct2);
  not not_57 (not_57_out, Funct4);
  not not_58 (not_58_out, Funct3);
  not not_59 (not_59_out, Funct1);
  not not_60 (not_60_out, Funct0);
  not not_61 (not_61_out, Funct4);
  not not_62 (not_62_out, Funct3);
  not not_63 (not_63_out, Funct1);
  not not_64 (not_64_out, Funct4);
  not not_65 (not_65_out, Funct3);
  not not_66 (not_66_out, OP5);
  not not_67 (not_67_out, OP4);
  not not_68 (not_68_out, OP3);
  not not_69 (not_69_out, OP2);
  not not_70 (not_70_out, OP1);
  not not_71 (not_71_out, OP0);
  not not_72 (not_72_out, Funct4);
  not not_73 (not_73_out, Funct3);
  not not_74 (not_74_out, Funct2);
  not not_75 (not_75_out, OP5);
  not not_76 (not_76_out, OP4);
  not not_77 (not_77_out, OP3);
  not not_78 (not_78_out, OP2);
  not not_79 (not_79_out, OP1);
  not not_80 (not_80_out, OP0);
  not not_81 (not_81_out, Funct4);
  not not_82 (not_82_out, Funct2);
  not not_83 (not_83_out, OP5);
  not not_84 (not_84_out, OP4);
  not not_85 (not_85_out, OP3);
  not not_86 (not_86_out, OP2);
  not not_87 (not_87_out, OP1);
  not not_88 (not_88_out, OP0);
  not not_89 (not_89_out, Funct4);
  not not_90 (not_90_out, Funct3);
  not not_91 (not_91_out, OP5);
  not not_92 (not_92_out, OP4);
  not not_93 (not_93_out, OP3);
  not not_94 (not_94_out, OP2);
  not not_95 (not_95_out, OP1);
  not not_96 (not_96_out, Funct4);
  not not_97 (not_97_out, Funct3);
  not not_98 (not_98_out, Funct2);
  not not_99 (not_99_out, OP5);
  not not_100 (not_100_out, OP4);
  not not_101 (not_101_out, OP2);
  not not_102 (not_102_out, OP0);
  not not_103 (not_103_out, OP5);
  not not_104 (not_104_out, OP4);
  not not_105 (not_105_out, OP3);
  not not_106 (not_106_out, OP2);
  not not_107 (not_107_out, OP1);
  not not_108 (not_108_out, OP0);
  not not_109 (not_109_out, Funct4);
  not not_110 (not_110_out, Funct3);
  not not_111 (not_111_out, Funct2);
  not not_112 (not_112_out, OP5);
  not not_113 (not_113_out, OP4);
  not not_114 (not_114_out, OP3);
  not not_115 (not_115_out, OP2);
  not not_116 (not_116_out, OP1);
  not not_117 (not_117_out, OP0);
  not not_118 (not_118_out, Funct4);
  not not_119 (not_119_out, Funct3);
  not not_120 (not_120_out, OP5);
  not not_121 (not_121_out, OP4);
  not not_122 (not_122_out, OP3);
  not not_123 (not_123_out, OP2);
  not not_124 (not_124_out, OP1);
  not not_125 (not_125_out, OP0);
  not not_126 (not_126_out, Funct4);
  not not_127 (not_127_out, Funct2);
  not not_128 (not_128_out, OP5);
  not not_129 (not_129_out, OP4);
  not not_130 (not_130_out, OP3);
  not not_131 (not_131_out, OP2);
  not not_132 (not_132_out, OP1);
  not not_133 (not_133_out, Funct4);
  not not_134 (not_134_out, Funct3);
  not not_135 (not_135_out, Funct2);
  not not_136 (not_136_out, OP5);
  not not_137 (not_137_out, OP4);
  not not_138 (not_138_out, OP1);
  and and_1 (and_1_out, not_1_out, not_2_out, not_3_out, not_4_out, not_5_out, not_6_out, not_7_out, Funct4, not_8_out, not_9_out, not_10_out, not_11_out);
  and and_2 (and_2_out, not_12_out, not_13_out, not_14_out, not_15_out, not_16_out, not_17_out, Funct5, not_18_out, not_19_out, not_20_out);
  and and_3 (and_3_out, not_21_out, not_22_out, not_23_out, not_24_out, not_25_out, not_26_out, Funct5, not_27_out, not_28_out, Funct0);
  and and_4 (and_4_out, not_29_out, not_30_out, not_31_out, not_32_out, not_33_out, not_34_out, Funct5, not_35_out, not_36_out, Funct1);
  and and_5 (and_5_out, not_37_out, not_38_out, not_39_out, not_40_out, not_41_out, Funct5, not_42_out, not_43_out, not_44_out, Funct1, Funct0);
  and and_6 (and_6_out, not_45_out, not_46_out, OP3, not_47_out, OP1, not_48_out);
  and and_7 (and_7_out, not_49_out, not_50_out, OP3, OP2, not_51_out);
  and and_8 (and_8_out, Funct5, not_52_out, Funct3, not_53_out, Funct1, not_54_out);
  and and_9 (and_9_out, Funct5, not_55_out, Funct3, not_56_out, Funct1, Funct0);
  not not_139 (not_139_out, OP5);
  not not_140 (not_140_out, OP4);
  not not_141 (not_141_out, OP2);
  not not_142 (not_142_out, OP0);
  and and_10 (and_10_out, Funct5, not_57_out, not_58_out, Funct2, not_59_out, not_60_out);
  and and_11 (and_11_out, Funct5, not_61_out, not_62_out, Funct2, not_63_out, Funct0);
  and and_12 (and_12_out, Funct5, not_64_out, not_65_out, Funct2, Funct1, Funct0);
  not not_143 (not_143_out, OP5);
  not not_144 (not_144_out, OP4);
  not not_145 (not_145_out, OP1);
  not not_146 (not_146_out, OP0);
  not not_147 (not_147_out, OP5);
  not not_148 (not_148_out, OP4);
  not not_149 (not_149_out, OP1);
  and and_13 (and_13_out, not_66_out, not_67_out, not_68_out, not_69_out, not_70_out, not_71_out, not_72_out, not_73_out, not_74_out, Funct1);
  and and_14 (and_14_out, not_75_out, not_76_out, not_77_out, not_78_out, not_79_out, not_80_out, Funct5, not_81_out, not_82_out, Funct1);
  and and_15 (and_15_out, not_83_out, not_84_out, not_85_out, not_86_out, not_87_out, not_88_out, Funct5, not_89_out, not_90_out, Funct1, Funct0);
  and and_16 (and_16_out, not_91_out, not_92_out, not_93_out, not_94_out, not_95_out, Funct5, not_96_out, not_97_out, not_98_out, Funct1, Funct0);
  and and_17 (and_17_out, not_99_out, not_100_out, OP3, not_101_out, OP1, not_102_out);
  and and_18 (and_18_out, not_103_out, not_104_out, not_105_out, not_106_out, not_107_out, not_108_out, not_109_out, not_110_out, not_111_out, Funct1, Funct0);
  and and_19 (and_19_out, not_112_out, not_113_out, not_114_out, not_115_out, not_116_out, not_117_out, Funct5, not_118_out, not_119_out, Funct0);
  and and_20 (and_20_out, not_120_out, not_121_out, not_122_out, not_123_out, not_124_out, not_125_out, Funct5, not_126_out, not_127_out, Funct1, Funct0);
  and and_21 (and_21_out, not_128_out, not_129_out, not_130_out, not_131_out, not_132_out, Funct5, not_133_out, not_134_out, not_135_out, Funct1, Funct0);
  and and_22 (and_22_out, not_136_out, not_137_out, OP3, OP2, not_138_out, OP0);
  or or_1 (funct_out5, and_1_out, and_2_out, and_3_out, and_4_out, and_5_out, and_6_out, and_7_out);
  nor nor_1 (nor_1_out, OP5, OP4, OP3, OP2, OP1, OP0);
  and and_23 (and_23_out, nor_1_out, or_2_out);
  or or_2 (or_2_out, and_8_out, and_9_out);
  and and_24 (and_24_out, not_139_out, not_140_out, OP3, not_141_out, OP1, not_142_out);
  nor nor_2 (nor_2_out, OP5, OP4, OP3, OP2, OP1, OP0);
  and and_25 (and_25_out, nor_2_out, or_3_out);
  or or_3 (or_3_out, and_10_out, and_11_out, and_12_out);
  and and_26 (and_26_out, not_143_out, not_144_out, OP3, OP2, not_145_out, not_146_out);
  and and_27 (and_27_out, not_147_out, not_148_out, OP3, OP2, not_149_out, OP0);
  or or_4 (funct_out1, and_13_out, and_14_out, and_15_out, and_16_out, and_17_out);
  or or_5 (funct_out0, and_18_out, and_19_out, and_20_out, and_21_out, and_22_out);
  or or_6 (funct_out3, and_23_out, and_24_out);
  or or_7 (funct_out2, and_25_out, and_26_out, and_27_out);

  assign funct_out4 = 1'b0;
endmodule

module aluin_control (
  input  ALUop1,
  input  ALUop0,
  input  Funct5,
  input  Funct4,
  input  Funct3,
  input  Funct2,
  input  Funct1,
  input  Funct0,
  output ALUin3,
  output ALUin2,
  output ALUin1,
  output ALUin0
);

  wire and_1_out, and_2_out, and_3_out, and_4_out, and_5_out, and_6_out, and_7_out, and_8_out, and_9_out,
       and_10_out, and_11_out, and_12_out, and_13_out, and_14_out, and_15_out, and_16_out, and_17_out,
       not_1_out, not_2_out, not_3_out, not_4_out, not_5_out, not_6_out, not_7_out, not_8_out, not_9_out,
       not_10_out, not_11_out, not_12_out, not_13_out, not_14_out, not_15_out, not_16_out, not_17_out,
       not_18_out, not_19_out, not_20_out, not_21_out, not_22_out, not_23_out, not_24_out, not_25_out,
       not_26_out, not_27_out, not_28_out, not_29_out, not_30_out, not_31_out, not_32_out, not_33_out,
       not_34_out, not_35_out, not_36_out, not_37_out, not_38_out, not_39_out, not_40_out, not_41_out,
       not_42_out, not_43_out, not_44_out, not_45_out, not_46_out, not_47_out, not_48_out, not_49_out,
       not_50_out, not_51_out, not_52_out, not_53_out, not_54_out, not_55_out, not_56_out, not_57_out,
       not_58_out, not_59_out, not_60_out, or_4_out;

  not not_1 (not_1_out, ALUop0);
  not not_2 (not_2_out, Funct4);
  not not_3 (not_3_out, Funct3);
  not not_4 (not_4_out, ALUop0);
  not not_5 (not_5_out, Funct4);
  not not_6 (not_6_out, Funct2);
  not not_7 (not_7_out, ALUop0);
  not not_8 (not_8_out, Funct4);
  not not_9 (not_9_out, Funct3);
  not not_10 (not_10_out, Funct2);
  not not_11 (not_11_out, ALUop0);
  not not_12 (not_12_out, Funct4);
  not not_13 (not_13_out, Funct3);
  not not_14 (not_14_out, Funct1);
  not not_15 (not_15_out, Funct0);
  not not_16 (not_16_out, ALUop0);
  not not_17 (not_17_out, Funct4);
  not not_18 (not_18_out, Funct2);
  not not_19 (not_19_out, ALUop1);
  not not_20 (not_20_out, ALUop0);
  not not_21 (not_21_out, Funct4);
  not not_22 (not_22_out, Funct3);
  not not_23 (not_23_out, Funct2);
  not not_24 (not_24_out, Funct0);
  not not_25 (not_25_out, ALUop0);
  not not_26 (not_26_out, Funct4);
  not not_27 (not_27_out, Funct2);
  not not_28 (not_28_out, Funct0);
  not not_29 (not_29_out, ALUop0);
  not not_30 (not_30_out, Funct4);
  not not_31 (not_31_out, Funct3);
  not not_32 (not_32_out, ALUop0);
  not not_33 (not_33_out, Funct4);
  not not_34 (not_34_out, Funct3);
  not not_35 (not_35_out, Funct1);
  not not_36 (not_36_out, Funct0);
  not not_37 (not_37_out, Funct4);
  not not_38 (not_38_out, Funct3);
  not not_39 (not_39_out, Funct2);
  not not_40 (not_40_out, Funct1);
  not not_41 (not_41_out, Funct0);
  not not_42 (not_42_out, Funct4);
  not not_43 (not_43_out, Funct3);
  not not_44 (not_44_out, Funct2);
  not not_45 (not_45_out, Funct1);
  not not_46 (not_46_out, Funct4);
  not not_47 (not_47_out, Funct3);
  not not_48 (not_48_out, Funct1);
  not not_49 (not_49_out, Funct0);
  not not_50 (not_50_out, Funct4);
  not not_51 (not_51_out, Funct2);
  not not_52 (not_52_out, Funct0);
  not not_53 (not_53_out, Funct5);
  not not_54 (not_54_out, Funct4);
  not not_55 (not_55_out, Funct3);
  not not_56 (not_56_out, Funct2);
  and and_1 (and_1_out, ALUop1, not_1_out, Funct5, not_2_out, not_3_out, Funct2, Funct0);
  and and_2 (and_2_out, ALUop1, not_4_out, Funct5, not_5_out, Funct3, not_6_out, Funct1);
  not not_57 (not_57_out, ALUop1);
  and and_3 (and_3_out, not_7_out, Funct5, not_8_out, not_9_out, not_10_out);
  and and_4 (and_4_out, not_11_out, Funct5, not_12_out, not_13_out, not_14_out, not_15_out);
  and and_5 (and_5_out, not_16_out, Funct5, not_17_out, not_18_out, Funct1, Funct0);
  and and_6 (and_6_out, not_19_out, ALUop0);
  and and_7 (and_7_out, ALUop1, not_20_out, not_21_out, not_22_out, not_23_out, Funct1, not_24_out);
  and and_8 (and_8_out, ALUop1, not_25_out, Funct5, not_26_out, not_27_out, Funct1, not_28_out);
  and and_9 (and_9_out, ALUop1, not_29_out, Funct5, not_30_out, not_31_out, Funct1, Funct0);
  and and_10 (and_10_out, ALUop1, not_32_out, Funct5, not_33_out, not_34_out, Funct2, not_35_out, not_36_out);
  and and_11 (and_11_out, Funct5, not_37_out, not_38_out, not_39_out, not_40_out, not_41_out);
  and and_12 (and_12_out, Funct5, not_42_out, not_43_out, not_44_out, not_45_out, Funct0);
  and and_13 (and_13_out, Funct5, not_46_out, not_47_out, Funct2, not_48_out, not_49_out);
  and and_14 (and_14_out, Funct5, not_50_out, Funct3, not_51_out, Funct1, not_52_out);
  and and_15 (and_15_out, not_53_out, not_54_out, not_55_out, not_56_out, Funct1, Funct0);
  or or_1 (ALUin3, and_1_out, and_2_out);
  or or_2 (ALUin2, not_57_out, and_3_out, and_4_out, and_5_out);
  or or_3 (ALUin1, and_6_out, and_7_out, and_8_out, and_9_out, and_10_out);
  not not_58 (not_58_out, ALUop0);
  or or_4 (or_4_out, and_11_out, and_12_out, and_13_out, and_14_out, and_15_out);
  not not_59 (not_59_out, ALUop1);
  not not_60 (not_60_out, ALUop0);
  and and_16 (and_16_out, ALUop1, not_58_out, or_4_out);
  or or_5 (ALUin0, and_16_out, and_17_out);
  and and_17 (and_17_out, not_59_out, not_60_out);
endmodule

module imme_extent (
  input  OP5,
  input  OP4,
  input  OP3,
  input  OP2,
  input  OP1,
  input  OP0,
  output extent_out
);

  wire and_1_out, and_2_out, and_3_out, and_4_out, not_1_out, not_2_out, not_3_out, not_4_out, not_5_out;

  not not_1 (not_1_out, OP5);
  not not_2 (not_2_out, OP3);
  not not_3 (not_3_out, OP2);
  not not_4 (not_4_out, OP0);
  not not_5 (not_5_out, OP3);
  and and_1 (and_1_out, not_1_out, not_2_out);
  and and_2 (and_2_out, not_3_out, not_4_out);
  and and_3 (and_3_out, not_5_out, OP0);
  and and_4 (and_4_out, OP5, OP3);
  or or_1 (extent_out, and_1_out, and_2_out, and_3_out, OP1, OP4, and_4_out);
endmodule

module Imme_extent (
  input  [5:0] OP,
  output extent_out
);

  imme_extent imme_extent_1 (
    .OP5(OP[5]), .OP4(OP[4]), .OP3(OP[3]), .OP2(OP[2]), .OP1(OP[1]), .OP0(OP[0]), .extent_out(extent_out));

  // Notes on the sheet:
  //   立即数拓展控制，无符号拓展时输出0，否则，输出1
endmodule

module bgez (
  input  OP5,
  input  OP4,
  input  OP3,
  input  OP2,
  input  OP1,
  input  OP0,
  input  BGEZ4,
  input  BGEZ3,
  input  BGEZ2,
  input  BGEZ1,
  input  BGEZ0,
  output Jump1,
  output Jump0,
  output Jump_select
);

  wire not_1_out, not_2_out, not_3_out, not_4_out, not_5_out, not_6_out, not_7_out, not_8_out, not_9_out,
       not_10_out, not_11_out, not_12_out, not_13_out, not_14_out, not_15_out, not_16_out, not_17_out,
       not_18_out, not_19_out, not_20_out, not_21_out, not_22_out, not_23_out, not_24_out, not_25_out,
       not_26_out, not_27_out;

  not not_1 (not_1_out, OP5);
  not not_2 (not_2_out, OP4);
  not not_3 (not_3_out, OP3);
  not not_4 (not_4_out, OP2);
  not not_5 (not_5_out, OP1);
  not not_6 (not_6_out, BGEZ4);
  not not_7 (not_7_out, BGEZ3);
  not not_8 (not_8_out, BGEZ2);
  not not_9 (not_9_out, BGEZ1);
  not not_10 (not_10_out, OP5);
  not not_11 (not_11_out, OP4);
  not not_12 (not_12_out, OP3);
  not not_13 (not_13_out, OP2);
  not not_14 (not_14_out, OP1);
  not not_15 (not_15_out, BGEZ4);
  not not_16 (not_16_out, BGEZ3);
  not not_17 (not_17_out, BGEZ2);
  not not_18 (not_18_out, BGEZ1);
  not not_19 (not_19_out, OP5);
  not not_20 (not_20_out, OP4);
  not not_21 (not_21_out, OP3);
  not not_22 (not_22_out, OP2);
  not not_23 (not_23_out, OP1);
  not not_24 (not_24_out, BGEZ4);
  not not_25 (not_25_out, BGEZ3);
  not not_26 (not_26_out, BGEZ2);
  not not_27 (not_27_out, BGEZ1);
  and and_1 (Jump1, not_1_out, not_2_out, not_3_out, not_4_out, not_5_out, OP0, not_6_out, not_7_out, not_8_out, not_9_out, BGEZ0);
  and and_2 (Jump0, not_10_out, not_11_out, not_12_out, not_13_out, not_14_out, OP0, not_15_out, not_16_out, not_17_out, not_18_out, BGEZ0);
  and and_3 (Jump_select, not_19_out, not_20_out, not_21_out, not_22_out, not_23_out, OP0, not_24_out, not_25_out, not_26_out, not_27_out, BGEZ0);
endmodule

module Bgez (
  input  [5:0] op,
  input  [4:0] rt,
  output [1:0] jump,
  output jump_control
);

  bgez bgez_1 (
    .OP5(op[5]), .OP4(op[4]), .OP3(op[3]), .OP2(op[2]), .OP1(op[1]), .OP0(op[0]), .BGEZ4(rt[4]),
    .BGEZ3(rt[3]), .BGEZ2(rt[2]), .BGEZ1(rt[1]), .BGEZ0(rt[0]), .Jump1(jump[1]), .Jump0(jump[0]),
    .Jump_select(jump_control));

  // Notes on the sheet:
  //   实现BGEZ指令
endmodule
