// Logisim project 王永辉_CS1405_U201414684_regfile.circ as structural Verilog: 4 circuits, main circuit main
module main (
  input  [4:0] Reg1_num,
  input  [4:0] Reg2,
  input  [4:0] Write_Reg_num,
  input  [31:0] Din,
  input  Write_Enable,
  input  Clock,
  output [31:0] Reg1,
  output [31:0] s0_Value,
  output [31:0] s1_Value,
  output [31:0] s2_Value,
  output [31:0] ra_Value,
  output [31:0] Reg2_2
);

  MyRegfile myregfile_1 (
    .WE(Write_Enable), .R1(Reg1), .R2(Reg2_2), .S0(s0_Value), .S1(s1_Value), .S2(s2_Value), .ra(ra_Value),
    .W_num(Write_Reg_num), .Din(Din), .R1_num(Reg1_num), .R2_num(Reg2), .CLK(Clock));

  // Other names for the same wires on the sheet: clk = Clock; ra[31:0] = ra_Value; reg2_num[4:0] = Reg2;
  //   reg2_t[31:0] = Reg2_2; s0[31:0] = s0_Value; s1[31:0] = s1_Value; s2[31:0] = s2_Value; WE = Write_Enable;
  //   write_data[31:0] = Din

  // Notes on the sheet:
  //   输入引脚
  //   输出引脚
  //   Debug引脚，便于观测寄存器值
  //   请勿修改引脚以及封装，直接使用隧道连接电路
endmodule

module test (
);

  wire undriven;

  main main_1 (.Clock(undriven));  // open: Reg1_num, Reg2, Write_Reg_num, Din, Write_Enable, Reg1, Reg2_2, s0_Value, s1_Value, s2_Value, ra_Value
endmodule

module MyRegfile (
  input  CLK,
  input  [31:0] Din,
  input  [4:0] W_num,
  input  [4:0] R1_num,
  input  WE,
  input  [4:0] R2_num,
  output [31:0] R1,
  output [31:0] R2,
  output [31:0] S0,
  output [31:0] S1,
  output [31:0] S2,
  output [31:0] ra
);

  wire demultiplexer_1_out0, demultiplexer_1_out1, demultiplexer_1_out2, demultiplexer_1_out3,
       demultiplexer_1_out4, demultiplexer_1_out5, demultiplexer_1_out6, demultiplexer_1_out7,
       demultiplexer_1_out8, demultiplexer_1_out9, demultiplexer_1_out10, demultiplexer_1_out11,
       demultiplexer_1_out12, demultiplexer_1_out13, demultiplexer_1_out14, demultiplexer_1_out15,
       demultiplexer_1_out16, demultiplexer_1_out17, demultiplexer_1_out18, demultiplexer_1_out19,
       demultiplexer_1_out20, demultiplexer_1_out21, demultiplexer_1_out22, demultiplexer_1_out23,
       demultiplexer_1_out24, demultiplexer_1_out25, demultiplexer_1_out26, demultiplexer_1_out27,
       demultiplexer_1_out28, demultiplexer_1_out29, demultiplexer_1_out30, demultiplexer_1_out31;
  wire [31:0] _0_q, _1_q, _2_q, _3_q, _4_q, _5_q, _6_q, _7_q, _8_q, _9_q, _10_q, _11_q, _12_q, _13_q, _14_q,
       _15_q, _19_q, _20_q, _21_q, _22_q, _23_q, _24_q, _25_q, _26_q, _27_q, _28_q, _29_q, _30_q;

  Demultiplexer #(.select(5), .enable("false")) demultiplexer_1 (
    .out0(demultiplexer_1_out0), .out1(demultiplexer_1_out1), .out2(demultiplexer_1_out2),
    .out3(demultiplexer_1_out3), .out4(demultiplexer_1_out4), .out5(demultiplexer_1_out5),
    .out6(demultiplexer_1_out6), .out7(demultiplexer_1_out7), .out8(demultiplexer_1_out8),
    .out9(demultiplexer_1_out9), .out10(demultiplexer_1_out10), .out11(demultiplexer_1_out11),
    .out12(demultiplexer_1_out12), .out13(demultiplexer_1_out13), .out14(demultiplexer_1_out14),
    .out15(demultiplexer_1_out15), .out16(demultiplexer_1_out16), .out17(demultiplexer_1_out17),
    .out18(demultiplexer_1_out18), .out19(demultiplexer_1_out19), .out20(demultiplexer_1_out20),
    .out21(demultiplexer_1_out21), .out22(demultiplexer_1_out22), .out23(demultiplexer_1_out23),
    .out24(demultiplexer_1_out24), .out25(demultiplexer_1_out25), .out26(demultiplexer_1_out26),
    .out27(demultiplexer_1_out27), .out28(demultiplexer_1_out28), .out29(demultiplexer_1_out29),
    .out30(demultiplexer_1_out30), .out31(demultiplexer_1_out31), .in(WE), .sel(W_num));
  Register #(.width(32)) _0 (.D(Din), .en(demultiplexer_1_out0), .Q(_0_q), .clk(CLK), .clr(1'b1));
  Register #(.width(32)) _1 (.D(Din), .en(demultiplexer_1_out1), .Q(_1_q), .clk(CLK), .clr(1'b0));
  Register #(.width(32)) _2 (.D(Din), .en(demultiplexer_1_out2), .Q(_2_q), .clk(CLK), .clr(1'b0));
  Register #(.width(32)) _3 (.D(Din), .en(demultiplexer_1_out3), .Q(_3_q), .clk(CLK), .clr(1'b0));
  Register #(.width(32)) _4 (.D(Din), .en(demultiplexer_1_out4), .Q(_4_q), .clk(CLK), .clr(1'b0));
  Register #(.width(32)) _5 (.D(Din), .en(demultiplexer_1_out5), .Q(_5_q), .clk(CLK), .clr(1'b0));
  Register #(.width(32)) _6 (.D(Din), .en(demultiplexer_1_out6), .Q(_6_q), .clk(CLK), .clr(1'b0));
  Register #(.width(32)) _7 (.D(Din), .en(demultiplexer_1_out7), .Q(_7_q), .clk(CLK), .clr(1'b0));
  Register #(.width(32)) _8 (.D(Din), .en(demultiplexer_1_out8), .Q(_8_q), .clk(CLK), .clr(1'b0));
  Register #(.width(32)) _9 (.D(Din), .en(demultiplexer_1_out9), .Q(_9_q), .clk(CLK), .clr(1'b0));
  Register #(.width(32)) _10 (.D(Din), .en(demultiplexer_1_out10), .Q(_10_q), .clk(CLK), .clr(1'b0));
  Register #(.width(32)) _11 (.D(Din), .en(demultiplexer_1_out11), .Q(_11_q), .clk(CLK), .clr(1'b0));
  Register #(.width(32)) _12 (.D(Din), .en(demultiplexer_1_out12), .Q(_12_q), .clk(CLK), .clr(1'b0));
  Register #(.width(32)) _13 (.D(Din), .en(demultiplexer_1_out13), .Q(_13_q), .clk(CLK), .clr(1'b0));
  Register #(.width(32)) _14 (.D(Din), .en(demultiplexer_1_out14), .Q(_14_q), .clk(CLK), .clr(1'b0));
  Register #(.width(32)) _15 (.D(Din), .en(demultiplexer_1_out15), .Q(_15_q), .clk(CLK), .clr(1'b0));
  Register #(.width(32)) _16 (.D(Din), .en(demultiplexer_1_out16), .Q(S0), .clk(CLK), .clr(1'b0));
  Register #(.width(32)) _17 (.D(Din), .en(demultiplexer_1_out17), .Q(S1), .clk(CLK), .clr(1'b0));
  Register #(.width(32)) _18 (.D(Din), .en(demultiplexer_1_out18), .Q(S2), .clk(CLK), .clr(1'b0));
  Register #(.width(32)) _19 (.D(Din), .en(demultiplexer_1_out19), .Q(_19_q), .clk(CLK), .clr(1'b0));
  Register #(.width(32)) _20 (.D(Din), .en(demultiplexer_1_out20), .Q(_20_q), .clk(CLK), .clr(1'b0));
  Register #(.width(32)) _21 (.D(Din), .en(demultiplexer_1_out21), .Q(_21_q), .clk(CLK), .clr(1'b0));
  Register #(.width(32)) _22 (.D(Din), .en(demultiplexer_1_out22), .Q(_22_q), .clk(CLK), .clr(1'b0));
  Register #(.width(32)) _23 (.D(Din), .en(demultiplexer_1_out23), .Q(_23_q), .clk(CLK), .clr(1'b0));
  Register #(.width(32)) _24 (.D(Din), .en(demultiplexer_1_out24), .Q(_24_q), .clk(CLK), .clr(1'b0));
  Register #(.width(32)) _25 (.D(Din), .en(demultiplexer_1_out25), .Q(_25_q), .clk(CLK), .clr(1'b0));
  Register #(.width(32)) _26 (.D(Din), .en(demultiplexer_1_out26), .Q(_26_q), .clk(CLK), .clr(1'b0));
  Register #(.width(32)) _27 (.D(Din), .en(demultiplexer_1_out27), .Q(_27_q), .clk(CLK), .clr(1'b0));
  Register #(.width(32)) _28 (.D(Din), .en(demultiplexer_1_out28), .Q(_28_q), .clk(CLK), .clr(1'b0));
  Register #(.width(32)) _29 (.D(Din), .en(demultiplexer_1_out29), .Q(_29_q), .clk(CLK), .clr(1'b0));
  Register #(.width(32)) _30 (.D(Din), .en(demultiplexer_1_out30), .Q(_30_q), .clk(CLK), .clr(1'b0));
  Register #(.width(32)) _31 (.D(Din), .en(demultiplexer_1_out31), .Q(ra), .clk(CLK), .clr(1'b0));
  Multiplexer #(.select(5), .width(32), .disabled(0), .enable("false")) multiplexer_1 (
    .in0(_0_q), .in1(_1_q), .in2(_2_q), .in3(_3_q), .in4(_4_q), .in5(_5_q), .in6(_6_q), .in7(_7_q),
    .in8(_8_q), .in9(_9_q), .in10(_10_q), .in11(_11_q), .in12(_12_q), .in13(_13_q), .in14(_14_q),
    .in15(_15_q), .in16(S0), .in17(S1), .in18(S2), .in19(_19_q), .in20(_20_q), .in21(_21_q), .in22(_22_q),
    .in23(_23_q), .in24(_24_q), .in25(_25_q), .in26(_26_q), .in27(_27_q), .in28(_28_q), .in29(_29_q),
    .in30(_30_q), .in31(ra), .out(R1), .sel(R1_num));
  Multiplexer #(.select(5), .width(32), .disabled(0), .enable("false")) multiplexer_2 (
    .in0(_0_q), .in1(_1_q), .in2(_2_q), .in3(_3_q), .in4(_4_q), .in5(_5_q), .in6(_6_q), .in7(_7_q),
    .in8(_8_q), .in9(_9_q), .in10(_10_q), .in11(_11_q), .in12(_12_q), .in13(_13_q), .in14(_14_q),
    .in15(_15_q), .in16(S0), .in17(S1), .in18(S2), .in19(_19_q), .in20(_20_q), .in21(_21_q), .in22(_22_q),
    .in23(_23_q), .in24(_24_q), .in25(_25_q), .in26(_26_q), .in27(_27_q), .in28(_28_q), .in29(_29_q),
    .in30(_30_q), .in31(ra), .out(R2), .sel(R2_num));
endmodule

module AutoC (
);

  wire and_1_out, and_2_out, Clk_out, counter_1_carry, nor_1_out, not_2_out, or_1_out;
  wire [0:0] not_1_out;
  wire [1:0] counter_2_q;
  wire [3:0] myregfile_1_s0, myregfile_1_s0_2, myregfile_1_s0_3, myregfile_1_s0_4, myregfile_1_s0_5,
       myregfile_1_s0_6, myregfile_1_s0_7, myregfile_1_s0_8;
  wire [5:0] counter_1_q;
  wire [5:5] xnor_1_out;
  wire [31:0] multiplexer_1_out, myalu_1_result, myregfile_1_s1, ram_1_data;

  Hex_Digit_Display hex_digit_display_1 (.value(myregfile_1_s0_7));  // open: dp
  Hex_Digit_Display hex_digit_display_2 (.value(myregfile_1_s0_8));  // open: dp
  Hex_Digit_Display hex_digit_display_3 (.value(myregfile_1_s0_6));  // open: dp
  or or_1 (or_1_out, counter_1_q[5], counter_1_q[4], counter_1_q[3], counter_1_q[1], counter_1_q[0], counter_1_q[2]);
  Counter #(.width(6), .max('h20), .ongoal("stay")) counter_1 (
    .load(1'b0), .D({6{1'b0}}), .count(1'b1), .Q(counter_1_q), .carry(counter_1_carry), .clk(nor_1_out),
    .clr(1'b0));
  Counter #(.width(2), .max('h3)) counter_2 (
    .load(1'b0), .D(2'b00), .count(1'b1), .Q(counter_2_q), .clk(Clk_out), .clr(counter_1_carry));  // open: carry
  Clock Clk (.out(Clk_out));
  Hex_Digit_Display hex_digit_display_4 (.value(myregfile_1_s0_4));  // open: dp
  Hex_Digit_Display hex_digit_display_5 (.value(myregfile_1_s0_5));  // open: dp
  // Probe on {xnor_1_out[5], counter_1_q[4:0]}
  xnor xnor_1 (xnor_1_out[5], counter_2_q[0], counter_2_q[1]);
  and and_1 (and_1_out, counter_2_q[0], counter_2_q[1]);
  Hex_Digit_Display hex_digit_display_6 (.value(myregfile_1_s0_3));  // open: dp
  nor nor_1 (nor_1_out, counter_2_q[0], counter_2_q[1]);
  Hex_Digit_Display hex_digit_display_7 (.value(myregfile_1_s0_2));  // open: dp
  Hex_Digit_Display hex_digit_display_8 (.value(myregfile_1_s0));  // open: dp
  RAM #(.addrWidth(6), .dataWidth(32)) ram_1 (
    .addr({xnor_1_out[5], counter_1_q[4:0]}), .data(ram_1_data), .sel(1'b1), .clk(nor_1_out), .ld(and_2_out),
    .clr(1'b0));
  and and_2 (and_2_out, not_1_out[0], counter_2_q[0]);
  not not_1 (not_1_out[0], counter_2_q[1]);
  assign ram_1_data = and_1_out ? myalu_1_result : 32'bz;  // Controlled_Buffer controlled_buffer_1
  MyALU myalu_1 (
    .X(multiplexer_1_out), .Y(myregfile_1_s1), .Result(myalu_1_result), .OP(4'b0101));  // open: UOF, OF, Equal, Result2
  Multiplexer #(.width(32), .disabled(0), .enable("false")) multiplexer_1 (
    .in0({32{1'b0}}),
    .in1({myregfile_1_s0_8, myregfile_1_s0_7, myregfile_1_s0_6, myregfile_1_s0_5, myregfile_1_s0_4, myregfile_1_s0_3, myregfile_1_s0_2, myregfile_1_s0}),
    .out(multiplexer_1_out), .sel(or_1_out));
  // Probe on myregfile_1_s1
  // Probe on {myregfile_1_s0_8, myregfile_1_s0_7, myregfile_1_s0_6, myregfile_1_s0_5, myregfile_1_s0_4, myregfile_1_s0_3, myregfile_1_s0_2, myregfile_1_s0}
  MyRegfile myregfile_1 (
    .WE(1'b1),
    .S0({myregfile_1_s0_8, myregfile_1_s0_7, myregfile_1_s0_6, myregfile_1_s0_5, myregfile_1_s0_4, myregfile_1_s0_3, myregfile_1_s0_2, myregfile_1_s0}),
    .S1(myregfile_1_s1), .W_num({4'b1000, not_1_out[0]}), .Din(ram_1_data), .R1_num({5{1'b0}}),
    .R2_num({5{1'b0}}), .CLK(not_2_out));  // open: R1, R2, S2, ra
  not not_2 (not_2_out, counter_2_q[0]);

  // Notes on the sheet:
  //   RAM
endmodule
